// Logisim project CPU Assembly 2026.circ as structural Verilog: 1 circuit, main circuit main
module main (
  input  [7:0] in_1,
  input  in_2,
  input  load_a,
  input  en_a,
  input  sub,
  input  add,
  input  en_alu,
  input  load_b,
  input  en_b,
  input  in_10
);

  wire alu2025_1_cout, clock_1_out, main_3_clock_out, reset_out;
  wire [7:0] alu2025_1_contents, controlled_buffer_1_out, main_1_internal_content, main_2_internal_content;

  // Probe on controlled_buffer_1_out
  assign controlled_buffer_1_out = in_2 ? in_1 : 8'bz;  // Controlled_Buffer controlled_buffer_1
  _8bit_reg_module_74_based_main main_1 (
    .internal_content(main_1_internal_content), .datain(controlled_buffer_1_out), .loadn(load_a),
    .clk(main_3_clock_out), .rst(reset_out), .oe(en_a), .bus(controlled_buffer_1_out));
  // Probe on main_1_internal_content
  // Probe on alu2025_1_contents
  // Probe on main_2_internal_content
  _8bit_reg_module_74_based_main main_2 (
    .internal_content(main_2_internal_content), .datain(controlled_buffer_1_out), .loadn(load_b),
    .clk(main_3_clock_out), .rst(reset_out), .oe(en_b), .bus(controlled_buffer_1_out));
  ALU2025 alu2025_1 (
    .Cout(alu2025_1_cout), .OUTPUT(controlled_buffer_1_out), .B(main_2_internal_content),
    .A(main_1_internal_content), .Sub_Cin(sub), .Add(add), .Mul(1'b0), .XOR(1'b0), .AND(1'b0), .OR(1'b0),
    .Bus_Enable(en_alu), .contents(alu2025_1_contents));
  // Probe on alu2025_1_cout
  Button reset (.out(reset_out));
  Clock_Module_main main_3 (.Clock_In(clock_1_out), .Halt(in_10), .Clock_Out(main_3_clock_out));
  Clock clock_1 (.out(clock_1_out));
endmodule
